// Digital circuit MUX_74151.dig as structural Verilog
module MUX_74151 (
  input  D,
  input  C,
  input  B,
  input  A,
  output Y
);

  wire _74151_1_pin2, not_1_out;

  not not_1 (not_1_out, A);
  _74151 _74151_1 (
    .pin1(not_1_out), .pin2(_74151_1_pin2), .pin3(D), .pin4(not_1_out), .pin5(Y), .pin7(1'b0), .pin8(1'b0),
    .pin12(A), .pin13(A), .pin14(_74151_1_pin2), .pin15(D), .pin16(1'b1));  // open: pin6, pin9, pin10, pin11
  not not_2 (_74151_1_pin2, D);

  // Notes on the sheet:
  //   74151 Multiplexer:
  //   C,B,A are select bits.  C is the MSB.
  //   D0-D7 are input data lines
  //   Y is the output
  //   W is the inverted output
  //   S is strobe.  When strobe is high the output is always low, 
  //     otherwise it's the selected data line.
  //   Inputs: Use A as the most-significant bit and 
  //   D as the least-significant bit.
endmodule

/* Test case:
A B C D Y
0 0 0 0 X
0 0 0 1 1
*/
